# Fritzing sketch Sensor Moduel 011023 (saved by Fritzing 1.0.0rc)
breadboards: 1

parts:
  Part1 = Arduino Uno (Rev3)
  M1 = Humidity and Temperature Sensor DHT11
  S1 = KY-026
  IC1 = MQ-2 [package="DIP (Dual Inline) [THT]"]
  A1 = PMS5003  # not connected
  A2 = ZP07 air quality detection module [part_number=esesdsa]

nets:
  N1: Part1.A5/SCL, IC1.pin4
  N2: Part1.D11_PWM/MOSI, S1.pin4
  N3: Part1.D2, A2.Pin_1
  N4: Part1.D4, M1.Data
  5V: Part1.5V, M1.Vcc, S1.pin3, IC1.pin1, A2.Pin_3
  GND: Part1.GND, M1.GND, S1.pin2, IC1.pin2, A2.Pin_4

notes:
  Linker
  Flame Sensor
  MQ-2
  Smoke Sensor
  DHT-11 Temperature & Humidity Sensor
  PMS7003 Laser PM2.5 Sensor

custom parts:
  Humidity and Temperature Sensor DHT11: Digital relative humidity & temperature sensor DHT11
  KY-026: ky-026 flame sensor module
  MQ-2: MQ-2 Gas Sensor module
  PMS5003: PMS5003 is a kind of digital and universal particle concentration sensor, which can be used to obtain the number of suspended particles in the air.
  ZP07 air quality detection module: ZP07 air-quality module adopts flat surface semiconductor gas sensor. The module has good sensitivity to volatile organic gases such as formaldehyde, benzene, carbon monoxide, ammonia, hydrogen, alcohol and smoke of cigarette, essence etc.
