# Fritzing sketch Sensor Moduel 260923 (saved by Fritzing 1.0.0rc)
breadboards: 1

parts:
  Part1 = Arduino Uno (Rev3)
  M1 = Humidity and Temperature Sensor DHT11
  A1 = PMS5003  # not connected
  S1 = KY-026
  IC1 = MQ-2 [package="DIP (Dual Inline) [THT]"]
  A2 = ZP07 air quality detection module [part_number=esesdsa]
  R1 = Resistor [tolerance=±5% power=0.25W resistance=220 package=THT]
  R2 = Resistor [tolerance=±5% power=0.25W resistance=220 package=THT]

nets:
  N1: Part1.A5/SCL, M1.Data
  N2: Part1.D9_PWM, R2.Pin_1
  N3: Part1.D10_PWM/SS, A2.Pin_1
  N4: Part1.D11_PWM/MOSI, S1.pin4
  N5: Part1.D2, IC1.pin4
  5V: Part1.5V, M1.Vcc, S1.pin3, IC1.pin1, A2.Pin_3
  GND: Part1.GND, M1.GND, S1.pin2, IC1.pin2, A2.Pin_4, R1.Pin_0
  N6: A2.Pin_2, R1.Pin_1, R2.Pin_0

notes:
  Linker
  Flame Sensor
  PM2.5
  Particulate Sensor
  MQ-2
  Smoke Sensor
  DHT-11 Temperature & Humidity Sensor

custom parts:
  Humidity and Temperature Sensor DHT11: Digital relative humidity & temperature sensor DHT11
  PMS5003: PMS5003 is a kind of digital and universal particle concentration sensor, which can be used to obtain the number of suspended particles in the air.
  KY-026: ky-026 flame sensor module
  MQ-2: MQ-2 Gas Sensor module
  ZP07 air quality detection module: ZP07 air-quality module adopts flat surface semiconductor gas sensor. The module has good sensitivity to volatile organic gases such as formaldehyde, benzene, carbon monoxide, ammonia, hydrogen, alcohol and smoke of cigarette, essence etc.
